// Logisim project TallerLogica-Combinatorios.circ as structural Verilog: 8 circuits, main circuit sumador_simple
module sumador_simple (
  input  a,
  input  b,
  output S,
  output Cout
);

  xor xor_1 (S, a, b);
  and and_1 (Cout, a, b);
endmodule

module sumador_completo (
  input  Cin,
  input  A,
  input  B,
  output S,
  output Cout
);

  wire and_1_out, and_2_out, xor_1_out;

  xor xor_1 (xor_1_out, A, B);
  and and_1 (and_1_out, A, B);
  and and_2 (and_2_out, Cin, xor_1_out);
  xor xor_2 (S, Cin, xor_1_out);
  or or_1 (Cout, and_2_out, and_1_out);
endmodule

module sumador_4 (
  input  Cin,
  input  [3:0] A,
  input  [3:0] B,
  output [3:0] S,
  output Cout
);

  wire adder_1_cout, adder_2_cout, adder_3_cout;

  Adder #(.width(1)) adder_1 (.a(A[0]), .b(B[0]), .out(S[0]), .cin(Cin), .cout(adder_1_cout));
  Adder #(.width(1)) adder_2 (.a(A[1]), .b(B[1]), .out(S[1]), .cin(adder_1_cout), .cout(adder_2_cout));
  Adder #(.width(1)) adder_3 (.a(A[2]), .b(B[2]), .out(S[2]), .cin(adder_2_cout), .cout(adder_3_cout));
  Adder #(.width(1)) adder_4 (.a(A[3]), .b(B[3]), .out(S[3]), .cin(adder_3_cout), .cout(Cout));
  Hex_Digit_Display hex_digit_display_1 (.value(S));  // open: dp

  // Notes on the sheet:
  //   Bit posicion 0
  //   Bit posicion 1
  //   Bit posicion 2
  //   Bit posicion 3
endmodule

module comparador_cero (
  input  [3:0] A,
  output Z
);

  wire and_1_out, nor_1_out, not_1_out, not_2_out;

  nor nor_1 (nor_1_out, A[0], A[1]);
  not not_1 (not_1_out, A[2]);
  and and_1 (and_1_out, nor_1_out, not_1_out);
  not not_2 (not_2_out, A[3]);
  and and_2 (Z, and_1_out, not_2_out);
endmodule

module sumador_flags (
  input  Cin,
  input  [3:0] A,
  input  [3:0] B,
  output [3:0] S,
  output N,
  output Z,
  output C,
  output V
);

  wire and_1_out, and_2_out, and_3_out, nor_1_out, not_1_out;

  sumador_4 sumador_4_1 (.Cin(Cin), .A(A), .S({N, S[2:0]}), .B(B), .Cout(C));
  nor nor_1 (nor_1_out, A[3], B[3]);
  not not_1 (not_1_out, N);
  and and_1 (and_1_out, A[3], B[3]);
  Hex_Digit_Display hex_digit_display_1 (.value({N, S[2:0]}));  // open: dp
  and and_2 (and_2_out, N, nor_1_out);
  and and_3 (and_3_out, not_1_out, and_1_out);
  comparador_cero comparador_cero_1 (.A({N, S[2:0]}), .Z(Z));
  or or_1 (V, and_2_out, and_3_out);

  assign S[3] = N;
endmodule

module incrementador_4 (
  input  [3:0] A,
  output [3:0] S
);

  sumador_4 sumador_4_1 (.Cin(1'b0), .A(4'b0001), .S(S), .B(A));  // open: Cout
  Hex_Digit_Display hex_digit_display_1 (.value(S));  // open: dp
endmodule

module inversor_4 (
  input  INV,
  input  [3:0] A,
  output [3:0] S
);

  wire [3:0] incrementador_4_1_s, not_1_out;

  not not_1 (not_1_out[0], A[0]);
  not not_2 (not_1_out[1], A[1]);
  not not_3 (not_1_out[2], A[2]);
  not not_4 (not_1_out[3], A[3]);
  incrementador_4 incrementador_4_1 (.A(not_1_out), .S(incrementador_4_1_s));
  Multiplexer #(.width(4), .enable("false")) multiplexer_1 (.in0(A), .in1(incrementador_4_1_s), .out(S), .sel(INV));
  Hex_Digit_Display hex_digit_display_1 (.value(S));  // open: dp
endmodule

module ALU (
  input  [3:0] A,
  input  [3:0] B,
  input  [1:0] OP,
  output C,
  output N,
  output Z,
  output V,
  output [3:0] S
);

  wire comparador_cero_1_z, comparador_cero_2_z, multiplexer_1_out, not_1_out, sumador_flags_1_c,
       sumador_flags_1_n, sumador_flags_1_z;
  wire [3:0] and_1_out, inversor_4_1_s, or_1_out, sumador_flags_1_s;

  Multiplexer #(.select(2), .enable("false")) multiplexer_1 (
    .in0(1'b0), .in1(1'b1), .in2(1'b0), .in3(1'b0), .out(multiplexer_1_out), .sel(OP));
  inversor_4 inversor_4_1 (.A(B), .INV(multiplexer_1_out), .S(inversor_4_1_s));
  sumador_flags sumador_flags_1 (
    .A(A), .B(inversor_4_1_s), .Cin(1'b0), .S(sumador_flags_1_s), .N(sumador_flags_1_n),
    .Z(sumador_flags_1_z), .C(sumador_flags_1_c), .V(V));
  and and_1 (and_1_out[0], A[0], B[0]);
  and and_2 (and_1_out[1], A[1], B[1]);
  and and_3 (and_1_out[2], A[2], B[2]);
  and and_4 (and_1_out[3], A[3], B[3]);
  or or_1 (or_1_out[0], A[0], B[0]);
  or or_2 (or_1_out[1], A[1], B[1]);
  or or_3 (or_1_out[2], A[2], B[2]);
  or or_4 (or_1_out[3], A[3], B[3]);
  not not_1 (not_1_out, sumador_flags_1_c);
  Multiplexer #(.select(2), .enable("false")) multiplexer_2 (
    .in0(sumador_flags_1_c), .in1(not_1_out), .in2(1'b0), .in3(1'b0), .out(C), .sel(OP));
  Multiplexer #(.select(2), .enable("false")) multiplexer_3 (
    .in0(sumador_flags_1_n), .in1(sumador_flags_1_n), .in2(and_1_out[3]), .in3(or_1_out[3]), .out(N), .sel(OP));
  Multiplexer #(.select(2), .width(4), .enable("false")) multiplexer_4 (
    .in0(sumador_flags_1_s), .in1(sumador_flags_1_s), .in2(and_1_out), .in3(or_1_out), .out(S), .sel(OP));
  comparador_cero comparador_cero_1 (.A(and_1_out), .Z(comparador_cero_1_z));
  comparador_cero comparador_cero_2 (.A(or_1_out), .Z(comparador_cero_2_z));
  Hex_Digit_Display hex_digit_display_1 (.value(S));  // open: dp
  Multiplexer #(.select(2), .enable("false")) multiplexer_5 (
    .in0(sumador_flags_1_z), .in1(sumador_flags_1_z), .in2(comparador_cero_1_z), .in3(comparador_cero_2_z),
    .out(Z), .sel(OP));
endmodule
