// Logisim project xd.circ as structural Verilog: 3 circuits, main circuit Registro simple
module Registro_simple (
  input  in_1,
  input  in_2,
  input  in_3,
  input  in_4,
  input  load,
  output out_6,
  output out_7,
  output out_8,
  output out_9
);

  wire and_1_out, clock_1_out;

  Clock clock_1 (.out(clock_1_out));
  and and_1 (and_1_out, clock_1_out, load);
  D_Flip_Flop d_ff_1 (.clk(and_1_out), .D(in_1), .Q(out_6));  // open: Qn, preset, en, reset
  D_Flip_Flop d_ff_2 (.clk(and_1_out), .D(in_2), .Q(out_7));  // open: Qn, preset, en, reset
  D_Flip_Flop d_ff_3 (.clk(and_1_out), .D(in_3), .Q(out_8));  // open: Qn, preset, en, reset
  D_Flip_Flop d_ff_4 (.clk(and_1_out), .D(in_4), .Q(out_9));  // open: Qn, preset, en, reset
endmodule

module Extensor_de_signo (
  input  in_1,
  output out_2,
  output out_3,
  output out_4,
  output out_5
);

  Registro_simple registro_simple_1 (.out_6(out_2), .out_7(out_3));  // open: in_1, in_2, in_3, in_4, load, out_8, out_9
  // AND_Gate and_1 is placed but not wired
  // AND_Gate and_2 is placed but not wired
  // AND_Gate and_3 is placed but not wired
  // OR_Gate or_1 has open pins: out=out_4
  // OR_Gate or_2 has open pins: out=out_5
endmodule

module salida_Restringida (
  input  in_1,
  input  in_2,
  input  in_3,
  input  in_4,
  input  in_5,
  input  in_6,
  output out_7,
  output out_8,
  output out_9,
  output out_10
);

  wire and_1_out, clock_1_out, registro_simple_1_out_6, registro_simple_1_out_7, registro_simple_1_out_8,
       registro_simple_1_out_9;

  Clock clock_1 (.out(clock_1_out));
  Registro_simple registro_simple_1 (
    .in_1(in_2), .in_2(in_3), .in_3(in_4), .in_4(in_6), .load(in_5), .out_6(registro_simple_1_out_6),
    .out_7(registro_simple_1_out_7), .out_8(registro_simple_1_out_8), .out_9(registro_simple_1_out_9));
  assign out_7 = and_1_out ? registro_simple_1_out_6 : 1'bz;  // Controlled_Buffer controlled_buffer_1
  assign out_8 = and_1_out ? registro_simple_1_out_7 : 1'bz;  // Controlled_Buffer controlled_buffer_2
  assign out_9 = and_1_out ? registro_simple_1_out_8 : 1'bz;  // Controlled_Buffer controlled_buffer_3
  assign out_10 = and_1_out ? registro_simple_1_out_9 : 1'bz;  // Controlled_Buffer controlled_buffer_4
  and and_1 (and_1_out, clock_1_out, in_1);
endmodule
